# Fritzing sketch wiringDiagram (saved by Fritzing 1.0.6)

parts:
  Part2 = InvenSense MPU6050
  Mod1 = L298N DC motor driver
  Mod2 = L298N DC motor driver
  J1 = XT60 Connector female [package=THT]
  M1 = gear-motor
  M2 = gear-motor
  M3 = gear-motor
  M4 = gear-motor
  Part1 = Arduino Uno (Rev3)

nets:
  VCC: Part2.VCC, Part1.5V
  GND: Part2.GND, Part1.GND
  N1: Part2.SCL, Part1.A5/SCL
  N2: Part2.SDA, Part1.A4/SDA
  N3: Mod1.OUT1, M1.pin_1
  N4: Mod1.OUT2, M1.pin_2
  12V: Mod1.12V, Mod1.5V-ENA-JMP-O, Mod2.12V, Mod2.5V-ENA-JMP-O, J1.VCC
  GND_2: Mod1.GND, Mod2.GND, J1.GND
  N5: Mod1.OUT3, M2.pin_2
  N6: Mod1.OUT4, M2.pin_1
  N7: Mod1.ENA, Part1.D3_PWM
  N8: Mod1.IN1, Part1.D2
  N9: Mod1.IN2, Part1.D4
  N10: Mod1.IN3, Part1.D7
  N11: Mod1.IN4, Part1.D8
  N12: Mod1.ENB, Part1.D5_PWM
  N13: Mod2.OUT1, M3.pin_1
  N14: Mod2.OUT2, M3.pin_2
  N15: Mod2.OUT3, M4.pin_2
  N16: Mod2.OUT4, M4.pin_1
  N17: Mod2.ENA, Part1.D6_PWM
  N18: Mod2.IN1, Part1.D10_PWM/SS
  N19: Mod2.IN2, Part1.D11_PWM/MOSI
  N20: Mod2.IN3, Part1.D12/MISO
  N21: Mod2.IN4, Part1.D13/SCK
  N22: Mod2.ENB, Part1.D9_PWM

custom parts:
  L298N DC motor driver: 2x DC motor driver with 78M05 positive voltage regulator (7..35 V) L298N: max 46 V, 2 A Set 5 V Enable jumper to enable 5 V regultor (needed for the L298N) and +5 V output at screw terminal or supply external +5 V at screw terminal Set ENA and/or ENB to +5 V to enable motor permanently or supply ENA and/or ENB with PWM signal IN1 and IN2 set rotation directory for motor A (OUT1/OUT2) IN2 and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
  XT60 Connector female: Yellow XT60 connector for high current loads up to 40A female
